# Fritzing sketch Schematic (saved by Fritzing 0.9.0b)
breadboards: 1
stripboards: 1

parts:
  U3 = Voltage Regulator - Variable [package="TO220 [THT]"]
  R1 = Resistor [tolerance=±5% resistance=220 package=THT]
  R2 = Resistor [tolerance=±5% resistance=121 package=THT]
  RHT1 = Humidity and Temperature Sensor RHT03
  U6 = RELAY [package=relay-jzc]
  Q1 = NPN-Transistor [package="TO92 [THT]"]
  R5 = Resistor [tolerance=±5% resistance=167 package=THT]
  U7 = ESP8266 WiFi Module [part_number=ESP8266]
  R6 = Resistor [tolerance=±5% resistance=1k package=THT]
  Programming_Iface = female pin header, 4 pins [form="♀ (female)"]
  R7 = Resistor [tolerance=±5% resistance=1k package=THT]
  R8 = Resistor [tolerance=±5% resistance=4.7k package=THT]
  D1 = Rectifier Diode [part_number=1N4001 package="300 mil [THT]"]
  LED1 = LED - 5mm [color="White (6500K)" package="5 mm [THT]"]

nets:
  N1: U3.ADJ, R1.Pin_0, R2.Pin_1
  3V3: U3.OUT, R1.Pin_1, RHT1.Vcc, U7.VCC, R6.Pin_0, R8.Pin_1
  5V: U3.IN, U6.COIL1, D1.cathode
  GND: R2.Pin_0, RHT1.GND_2, Q1.E, U7.GND, U7.GPIO_15, Programming_Iface.pin1, LED1.cathode
  N2: RHT1.Data-signal, U7.GPIO_2, R8.Pin_0
  N3: U6.COIL2, Q1.C, D1.anode
  N4: Q1.B, R5.Pin_1
  N5: R5.Pin_0, U7.GPIO_13
  N6: U7.RXD, Programming_Iface.pin3
  N7: U7.GPIO_0, R7.Pin_1
  N8: U7.CH_PD, R6.Pin_1
  N9: U7.TXD, Programming_Iface.pin4
  N10: U7.GPIO_12, LED1.anode
  N11: Programming_Iface.pin2, R7.Pin_0
